// Logisim project umips.circ as structural Verilog: 2 circuits, main circuit main
module main (
  output [15:0] Reg0,
  output [15:0] Reg1,
  output [15:0] Reg2,
  output [15:0] Reg3,
  output [15:0] Reg4,
  output [15:0] Reg5,
  output [15:0] Reg6,
  output [15:0] Reg7,
  output [3:0] Output3,
  output [3:0] Output2,
  output [3:0] Output1,
  output [3:0] Output0,
  output halt
);

  wire ALU_Src, and_3_out, Clock, comparator_1_eq, comparator_2_eq, decoder_3_out4, decoder_3_out5, GT,
       is_branch, is_jump, Jal, jr, jump, LI, LT, MemWrite, multiplexer_6_out, multiplexer_7_out,
       multiplexer_8_out, multiplexer_10_out, not_1_p2, not_2_p2, op_addui, Pc_Src, Put, RegWrite, WriteHILO,
       Z;
  wire [1:0] BranchType, MemtoReg;
  wire [2:0] ALU_Op;
  wire [3:0] Func;
  wire [7:0] JumpAddress, multiplexer_1_out, PC_1, PC_q;
  wire [7:3] Immediate;
  wire [15:0] ALU_Res, bit_extender_1_out, bit_extender_2_out, DataA, DataB, main_1_readdata1, main_2_hi,
       main_2_lo, multiplexer_5_out, multiplexer_9_out, ram_1_data, register_1_q, register_2_q, WDataA;
  wire [15:9] Instruction;

  Decoder #(.select(4)) decoder_1 (
    .out10(jr), .sel(Func));  // open: out0, out1, out2, out3, out4, out5, out6, out7, out8, out9, out11, out12, out13, out14, out15, en
  Decoder #(.select(4)) decoder_2 (
    .out1(LI), .out4(jump), .sel(Instruction[15:12]));  // open: out0, out2, out3, out5, out6, out7, out8, out9, out10, out11, out12, out13, out14, out15, en
  and and_1 (Jal, jump, is_jump, Func[0]);
  // NOT_Gate not_1: pin names not known; wires that end beside it: halt, not_1_p2
  Clock clock_1 (.out(Clock));
  Register PC (.D(multiplexer_1_out), .en(not_1_p2), .Q(PC_q), .clk(Clock));  // open: clr
  Adder adder_1 (.a(PC_q), .b(8'h1), .out(PC_1), .cin(1'b0));  // open: cout
  Multiplexer #(.width(8)) multiplexer_1 (
    .in0(PC_1), .in1(JumpAddress), .out(multiplexer_1_out), .sel(Pc_Src));  // open: en
  Multiplexer #(.width(16)) multiplexer_2 (
    .in0(multiplexer_9_out), .in1(bit_extender_1_out), .out(WDataA), .sel(Jal));  // open: en
  assign bit_extender_1_out = {{8{1'b0}}, PC_1};  // Bit_Extender bit_extender_1
  ROM #(.dataWidth(16)) rom_1 (.addr(PC_q), .data({Instruction, Immediate, Func}), .sel(1'b1));
  Comparator #(.width(1)) comparator_1 (.a(Func[0]), .b(1'b0), .eq(comparator_1_eq));  // open: gt, lt
  Comparator #(.width(4)) comparator_2 (.a(Instruction[15:12]), .b(4'b0000), .eq(comparator_2_eq));  // open: gt, lt
  RegFile_main main_1 (
    .ReadData0(DataA), .ReadData1(main_1_readdata1), .Reg0(Reg0), .Reg1(Reg1), .Reg2(Reg2), .Reg3(Reg3),
    .Reg4(Reg4), .Reg5(Reg5), .Reg6(Reg6), .Reg7(Reg7), .WriteData0(WDataA),
    .WriteSelect0(Instruction[11:9]), .ReadSelect0(Instruction[11:9]), .ReadSelect1(Immediate[7:5]),
    .WE0(RegWrite), .Clock(Clock));
  and and_2 (op_addui, comparator_1_eq, comparator_2_eq);
  Multiplexer #(.width(8)) multiplexer_3 (
    .in0({Immediate, Func[3:1]}), .in1(DataA[7:0]), .out(JumpAddress), .sel(jr));  // open: en
  Multiplexer #(.width(16)) multiplexer_4 (
    .in0(main_1_readdata1), .in1(bit_extender_2_out), .out(DataB), .sel(ALU_Src));  // open: en
  assign bit_extender_2_out = {{8{multiplexer_10_out}}, {Immediate, Func[3:1]}};  // Bit_Extender bit_extender_2
  Control_Unit control_unit_1 (
    .in_1({Instruction, Immediate, Func}), .out_2(BranchType), .out_3(Put), .out_4(RegWrite),
    .out_5(ALU_Src), .out_6(ALU_Op), .out_7(halt), .out_8(is_jump), .out_9(MemWrite), .out_10(is_branch),
    .out_11(MemtoReg));
  Multiplexer #(.width(16)) multiplexer_5 (
    .in0(DataA), .in1({16{1'b0}}), .out(multiplexer_5_out), .sel(LI));  // open: en
  ALU_main main_2 (
    .ALUOp(ALU_Op), .A(multiplexer_5_out), .B(DataB), .Result(ALU_Res), .GT(GT), .Zero(Z), .LT(LT),
    .in_4(Clock), .HI(main_2_hi), .LO(main_2_lo));
  // NOT_Gate not_2: pin names not known; wires that end beside it: Z, not_2_p2
  Multiplexer multiplexer_6 (.in0(1'b0), .in1(1'b1), .out(multiplexer_6_out), .sel(Immediate[7]));  // open: en
  Multiplexer multiplexer_7 (.in0(multiplexer_6_out), .in1(1'b0), .out(multiplexer_7_out), .sel(LI));  // open: en
  and and_3 (and_3_out, is_branch, multiplexer_8_out);
  Multiplexer #(.select(2)) multiplexer_8 (
    .in0(GT), .in1(LT), .in2(not_2_p2), .in3(Z), .out(multiplexer_8_out), .sel(BranchType));  // open: en
  Multiplexer #(.select(2), .width(16)) multiplexer_9 (
    .in0(ALU_Res), .in1(ram_1_data), .in2(register_2_q), .in3(register_1_q), .out(multiplexer_9_out),
    .sel(MemtoReg));  // open: en
  RAM #(.dataWidth(16), .bus("separate")) ram_1 (
    .addr(main_1_readdata1[7:0]), .din(DataA), .data(ram_1_data), .str(MemWrite), .sel(1'b1), .clk(Clock),
    .ld(1'b1));  // open: clr
  Multiplexer multiplexer_10 (
    .in0(multiplexer_7_out), .in1(1'b0), .out(multiplexer_10_out), .sel(op_addui));  // open: en
  or or_1 (Pc_Src, and_3_out, is_jump);
  Register #(.width(16), .trigger("high")) register_1 (
    .D(main_2_lo), .en(WriteHILO), .Q(register_1_q), .clk(Clock));  // open: clr
  Register #(.width(16), .trigger("high")) register_2 (
    .D(main_2_hi), .en(WriteHILO), .Q(register_2_q), .clk(Clock));  // open: clr
  Decoder #(.select(3)) decoder_3 (
    .out4(decoder_3_out4), .out5(decoder_3_out5), .sel(ALU_Op));  // open: out0, out1, out2, out3, out6, out7, en
  Register #(.width(16)) register_3 (
    .D(DataA), .en(Put), .Q({Output3, Output2, Output1, Output0}), .clk(Clock));  // open: clr
  or or_2 (WriteHILO, decoder_3_out4, decoder_3_out5);
  Hex_Digit_Display hex_digit_display_1 (.value(Output3));  // open: dp
  Hex_Digit_Display hex_digit_display_2 (.value(Output2));  // open: dp
  Hex_Digit_Display hex_digit_display_3 (.value(Output0));  // open: dp
  Hex_Digit_Display hex_digit_display_4 (.value(Output1));  // open: dp
  LED led_1 (.in(halt));

  // Other names for the same wires on the sheet: Instruction[8:0] = {Immediate, Func}; Subop = Func[0];
  //   Immediate[2:0] = Func[3:1]; Rt[2:0] = Immediate[7:5]; Immediate_MSB = Immediate[7]; Rs[2:0] = Instruction[11:9];
  //   Opcode[3:0] = Instruction[15:12]

  // Notes on the sheet:
  //   You must connect Reg0..7 to the top ports of the register file.
  //   Connect Output3..0 to your LED display.
  //   Output3 is the most significant
  //   Connect halt to your halt LED
endmodule

// Control
module Control_Unit (
  input  [15:0] in_1,
  output [1:0] out_2,
  output out_3,
  output out_4,
  output out_5,
  output [2:0] out_6,
  output out_7,
  output out_8,
  output out_9,
  output out_10,
  output [1:0] out_11
);

  wire add, \and , and_5_out, and_6_out, and_7_out, and_8_out, decoder_1_out8, decoder_1_out12, div,
       is_Rtype, jr, Math, mfhi, mflo, mul, \nor , not_1_p2, op_addi_addui, op_is_jump, op_j, op_jal, op_li,
       op_lw, or_1_out, or_6_out, or_7_out, or_8_out, sllv, srlv, sub;
  wire [2:0] or_11_out;

  and and_1 (op_jal, in_1[0], op_is_jump);
  and and_2 (op_j, not_1_p2, op_is_jump);
  // NOT_Gate not_1: pin names not known; wires that end beside it: in_1[0], not_1_p2
  and and_3 (Math, or_1_out, or_1_out);
  Decoder #(.select(4)) decoder_1 (
    .out0(op_addi_addui), .out1(op_li), .out4(op_is_jump), .out8(decoder_1_out8), .out12(decoder_1_out12),
    .out13(out_7), .out15(is_Rtype), .sel(in_1[15:12]));  // open: out2, out3, out5, out6, out7, out9, out10, out11, out14, en
  or or_1 (or_1_out, add, sub, \nor , \and , sllv, srlv, div, mflo, mfhi, op_lw);
  and and_4 (op_jal, in_1[0], out_8);
  or or_2 (out_10, decoder_1_out8, decoder_1_out12);
  and and_5 (and_5_out, jr, is_Rtype);
  or or_3 (out_8, op_is_jump, op_j, and_5_out);
  or or_4 (out_4, op_addi_addui, op_addi_addui, Math, op_li, op_jal);
  or or_5 (out_5, op_addi_addui, out_10, op_li);
  Decoder #(.select(4)) decoder_2 (
    .out0(add), .out1(sub), .out2(\nor ), .out3(\and ), .out4(sllv), .out5(srlv), .out6(div), .out7(mul),
    .out10(jr), .out11(out_3), .out12(mflo), .out13(mfhi), .out14(out_9), .out15(op_lw), .sel(in_1[3:0]));  // open: out8, out9, en
  or or_6 (or_6_out, 1'b0, op_lw);
  or or_7 (or_7_out, 1'b0, and_6_out);
  and and_6 (and_6_out, mfhi, is_Rtype);
  or or_8 (or_8_out, 1'b0, and_7_out);
  and and_7 (and_7_out, mflo, is_Rtype);
  and and_8 (and_8_out, or_6_out, is_Rtype);
  Multiplexer #(.width(3)) multiplexer_1 (.in0(3'b010), .in1(or_11_out), .out(out_6), .sel(is_Rtype));  // open: en
  Priority_Encoder #(.select(2)) priority_encoder_1 (
    .in0(1'b1), .in1(and_8_out), .in2(or_7_out), .in3(or_8_out), .out(out_11));  // open: gs, en_out, en_in
  or or_9 (or_11_out[2], mul, sllv, srlv, div);
  or or_10 (or_11_out[1], out_9, add, sub, sllv, srlv, op_lw);
  or or_11 (or_11_out[0], \nor , sub, div, srlv);

  assign out_2 = {in_1[14], in_1[0]};

  // Other names for the same wires on the sheet: ALUOp[2:0] = out_6; ALUSrc = out_5; Halt = out_7;
  //   BranchType[1:0] = {in_1[14], in_1[0]}; Func[3:0] = in_1[3:0]; Instruction[15:0] = in_1; Subop = in_1[0];
  //   Immediate[7:0] = in_1[8:1]; Rt[2:0] = in_1[8:6]; Rs[2:0] = in_1[11:9]; Opcode[3:0] = in_1[15:12];
  //   is_branch = out_10; is_jump = out_8; MemToReg[1:0] = out_11; op_put = out_3; Put = out_3; MemWrite = out_9;
  //   op_sw = out_9; RegWrite = out_4
endmodule
